// Logisim project chall.circ as structural Verilog: 1 circuit, main circuit main
module main (
  input  in_1
);

  wire xor_19_out;
  wire [3:0] multiplexer_1_out, multiplexer_2_out, multiplexer_3_out, multiplexer_4_out, multiplexer_5_out,
       multiplexer_6_out, multiplexer_7_out, multiplexer_8_out, multiplexer_9_out, multiplexer_10_out,
       multiplexer_11_out, multiplexer_12_out, multiplexer_13_out, multiplexer_14_out, multiplexer_15_out,
       multiplexer_16_out, multiplexer_17_out, multiplexer_18_out, multiplexer_19_out, multiplexer_20_out,
       multiplexer_21_out, multiplexer_22_out, multiplexer_23_out, multiplexer_24_out, multiplexer_25_out,
       multiplexer_26_out, multiplexer_27_out, multiplexer_28_out, multiplexer_29_out, multiplexer_30_out,
       multiplexer_31_out, multiplexer_32_out, multiplexer_33_out, multiplexer_34_out, multiplexer_35_out,
       multiplexer_36_out, multiplexer_37_out, multiplexer_38_out, multiplexer_39_out, multiplexer_40_out,
       multiplexer_41_out, multiplexer_42_out, multiplexer_43_out, multiplexer_44_out, multiplexer_45_out,
       multiplexer_46_out, multiplexer_47_out, multiplexer_48_out, multiplexer_49_out, multiplexer_50_out,
       multiplexer_51_out, multiplexer_52_out, multiplexer_53_out, multiplexer_54_out, multiplexer_55_out,
       multiplexer_56_out, multiplexer_57_out, multiplexer_58_out, multiplexer_59_out, multiplexer_60_out,
       multiplexer_61_out, multiplexer_62_out, multiplexer_63_out, multiplexer_64_out, multiplexer_65_out,
       multiplexer_66_out, multiplexer_67_out, multiplexer_68_out, multiplexer_69_out, multiplexer_70_out,
       multiplexer_71_out, multiplexer_72_out, multiplexer_73_out, multiplexer_74_out, multiplexer_75_out,
       multiplexer_76_out, multiplexer_77_out, multiplexer_78_out, multiplexer_79_out, multiplexer_80_out,
       multiplexer_81_out, multiplexer_82_out, multiplexer_83_out, multiplexer_84_out, multiplexer_85_out,
       multiplexer_86_out, multiplexer_87_out, multiplexer_88_out, multiplexer_89_out, multiplexer_90_out,
       multiplexer_91_out, multiplexer_92_out, multiplexer_93_out, multiplexer_94_out, multiplexer_95_out,
       multiplexer_96_out, multiplexer_97_out, multiplexer_98_out, multiplexer_99_out, multiplexer_100_out,
       multiplexer_101_out, multiplexer_102_out, multiplexer_103_out, multiplexer_104_out,
       multiplexer_105_out, multiplexer_106_out, multiplexer_107_out, multiplexer_108_out,
       multiplexer_109_out, multiplexer_110_out, multiplexer_111_out, multiplexer_112_out,
       multiplexer_113_out, multiplexer_114_out, multiplexer_115_out, multiplexer_116_out,
       multiplexer_117_out, multiplexer_118_out, multiplexer_119_out, multiplexer_120_out,
       multiplexer_121_out, multiplexer_122_out, multiplexer_123_out, multiplexer_124_out,
       multiplexer_125_out, multiplexer_126_out, multiplexer_127_out, multiplexer_128_out,
       multiplexer_129_out, multiplexer_130_out, multiplexer_131_out, multiplexer_132_out,
       multiplexer_133_out, multiplexer_134_out, multiplexer_135_out, multiplexer_136_out, or_1_out,
       undriven_35;
  wire [31:0] not_1_out, not_2_out, not_3_out, undriven, undriven_2, undriven_3, undriven_4, undriven_5,
       undriven_6, undriven_7, undriven_8, undriven_9, undriven_10, undriven_11, undriven_12, undriven_13,
       undriven_14, undriven_15, undriven_16, undriven_17, undriven_18, undriven_19, undriven_20,
       undriven_21, undriven_22, undriven_23, undriven_24, undriven_25, undriven_26, undriven_27,
       undriven_28, undriven_29, undriven_30, undriven_31, undriven_32, undriven_33, undriven_34,
       undriven_36, undriven_37, undriven_38, undriven_39, undriven_40, undriven_41, undriven_42,
       undriven_43, undriven_44, undriven_45, undriven_46, undriven_47, undriven_48, undriven_49,
       undriven_50, undriven_51, undriven_52, xor_1_out, xor_2_out, xor_3_out, xor_4_out, xor_5_out,
       xor_6_out, xor_7_out, xor_8_out, xor_9_out, xor_10_out, xor_11_out, xor_12_out, xor_13_out,
       xor_14_out, xor_15_out, xor_16_out, xor_17_out, xor_20_out, xor_21_out, xor_22_out, xor_23_out,
       xor_24_out, xor_25_out, xor_26_out, xor_27_out, xor_28_out, xor_29_out, xor_30_out, xor_31_out,
       xor_32_out, xor_33_out, xor_34_out, xor_35_out, xor_36_out;

  assign xor_1_out = undriven ^ undriven_2;  // XOR_Gate xor_1, 32 bits wide
  assign xor_2_out = undriven_3 ^ undriven_4;  // XOR_Gate xor_2, 32 bits wide
  assign xor_3_out = undriven_5 ^ undriven_6;  // XOR_Gate xor_3, 32 bits wide
  assign xor_4_out = undriven_7 ^ undriven_8;  // XOR_Gate xor_4, 32 bits wide
  assign xor_5_out = undriven_9 ^ undriven_10;  // XOR_Gate xor_5, 32 bits wide
  assign xor_6_out = undriven_11 ^ undriven_12;  // XOR_Gate xor_6, 32 bits wide
  assign xor_7_out = undriven_13 ^ undriven_14;  // XOR_Gate xor_7, 32 bits wide
  assign xor_8_out = undriven_15 ^ undriven_16;  // XOR_Gate xor_8, 32 bits wide
  assign xor_9_out = undriven_17 ^ undriven_18;  // XOR_Gate xor_9, 32 bits wide
  assign xor_10_out = undriven_19 ^ undriven_20;  // XOR_Gate xor_10, 32 bits wide
  assign xor_11_out = undriven_21 ^ undriven_22;  // XOR_Gate xor_11, 32 bits wide
  assign xor_12_out = undriven_23 ^ undriven_24;  // XOR_Gate xor_12, 32 bits wide
  assign xor_13_out = undriven_25 ^ undriven_26;  // XOR_Gate xor_13, 32 bits wide
  assign xor_14_out = undriven_27 ^ undriven_28;  // XOR_Gate xor_14, 32 bits wide
  assign xor_15_out = undriven_29 ^ undriven_30;  // XOR_Gate xor_15, 32 bits wide
  assign xor_16_out = undriven_31 ^ undriven_32;  // XOR_Gate xor_16, 32 bits wide
  assign xor_17_out = undriven_33 ^ undriven_34;  // XOR_Gate xor_17, 32 bits wide
  Multiplexer #(.width(4)) multiplexer_1 (.in0(xor_9_out[3:0]), .out(multiplexer_1_out), .sel(in_1));  // open: in1
  Multiplexer #(.width(4)) multiplexer_2 (
    .in0(xor_9_out[3:0]), .in1(xor_9_out[7:4]), .out(multiplexer_2_out), .sel(in_1));
  Multiplexer #(.width(4)) multiplexer_3 (
    .in0(xor_9_out[7:4]), .in1(xor_9_out[11:8]), .out(multiplexer_3_out), .sel(in_1));
  Multiplexer #(.width(4)) multiplexer_4 (
    .in0(xor_9_out[11:8]), .in1(xor_9_out[15:12]), .out(multiplexer_4_out), .sel(in_1));
  Multiplexer #(.width(4)) multiplexer_5 (
    .in0(xor_9_out[15:12]), .in1(xor_9_out[19:16]), .out(multiplexer_5_out), .sel(in_1));
  Multiplexer #(.width(4)) multiplexer_6 (
    .in0(xor_9_out[19:16]), .in1(xor_9_out[23:20]), .out(multiplexer_6_out), .sel(in_1));
  Multiplexer #(.width(4)) multiplexer_7 (
    .in0(xor_9_out[23:20]), .in1(xor_9_out[27:24]), .out(multiplexer_7_out), .sel(in_1));
  Multiplexer #(.width(4)) multiplexer_8 (
    .in0(xor_9_out[27:24]), .in1(xor_9_out[31:28]), .out(multiplexer_8_out), .sel(in_1));
  Multiplexer #(.width(4)) multiplexer_9 (
    .in0(xor_9_out[31:28]), .in1(xor_10_out[3:0]), .out(multiplexer_9_out), .sel(in_1));
  Multiplexer #(.width(4)) multiplexer_10 (
    .in0(xor_10_out[3:0]), .in1(xor_10_out[7:4]), .out(multiplexer_10_out), .sel(in_1));
  Multiplexer #(.width(4)) multiplexer_11 (
    .in0(xor_10_out[7:4]), .in1(xor_10_out[11:8]), .out(multiplexer_11_out), .sel(in_1));
  Multiplexer #(.width(4)) multiplexer_12 (
    .in0(xor_10_out[11:8]), .in1(xor_10_out[15:12]), .out(multiplexer_12_out), .sel(in_1));
  Multiplexer #(.width(4)) multiplexer_13 (
    .in0(xor_10_out[15:12]), .in1(xor_10_out[19:16]), .out(multiplexer_13_out), .sel(in_1));
  Multiplexer #(.width(4)) multiplexer_14 (
    .in0(xor_10_out[19:16]), .in1(xor_10_out[23:20]), .out(multiplexer_14_out), .sel(in_1));
  Multiplexer #(.width(4)) multiplexer_15 (
    .in0(xor_10_out[23:20]), .in1(xor_10_out[27:24]), .out(multiplexer_15_out), .sel(in_1));
  Multiplexer #(.width(4)) multiplexer_16 (
    .in0(xor_10_out[27:24]), .in1(xor_10_out[31:28]), .out(multiplexer_16_out), .sel(in_1));
  Multiplexer #(.width(4)) multiplexer_17 (
    .in0(xor_10_out[31:28]), .in1(xor_11_out[3:0]), .out(multiplexer_17_out), .sel(in_1));
  Multiplexer #(.width(4)) multiplexer_18 (
    .in0(xor_11_out[3:0]), .in1(xor_11_out[7:4]), .out(multiplexer_18_out), .sel(in_1));
  Multiplexer #(.width(4)) multiplexer_19 (
    .in0(xor_11_out[7:4]), .in1(xor_11_out[11:8]), .out(multiplexer_19_out), .sel(in_1));
  Multiplexer #(.width(4)) multiplexer_20 (
    .in0(xor_11_out[11:8]), .in1(xor_11_out[15:12]), .out(multiplexer_20_out), .sel(in_1));
  Multiplexer #(.width(4)) multiplexer_21 (
    .in0(xor_11_out[15:12]), .in1(xor_11_out[19:16]), .out(multiplexer_21_out), .sel(in_1));
  Multiplexer #(.width(4)) multiplexer_22 (
    .in0(xor_11_out[19:16]), .in1(xor_11_out[23:20]), .out(multiplexer_22_out), .sel(in_1));
  Multiplexer #(.width(4)) multiplexer_23 (
    .in0(xor_11_out[23:20]), .in1(xor_11_out[27:24]), .out(multiplexer_23_out), .sel(in_1));
  Multiplexer #(.width(4)) multiplexer_24 (
    .in0(xor_11_out[27:24]), .in1(xor_11_out[31:28]), .out(multiplexer_24_out), .sel(in_1));
  Multiplexer #(.width(4)) multiplexer_25 (
    .in0(xor_11_out[31:28]), .in1(xor_12_out[3:0]), .out(multiplexer_25_out), .sel(in_1));
  Multiplexer #(.width(4)) multiplexer_26 (
    .in0(xor_12_out[3:0]), .in1(xor_12_out[7:4]), .out(multiplexer_26_out), .sel(in_1));
  Multiplexer #(.width(4)) multiplexer_27 (
    .in0(xor_12_out[7:4]), .in1(xor_12_out[11:8]), .out(multiplexer_27_out), .sel(in_1));
  Multiplexer #(.width(4)) multiplexer_28 (
    .in0(xor_12_out[11:8]), .in1(xor_12_out[15:12]), .out(multiplexer_28_out), .sel(in_1));
  Multiplexer #(.width(4)) multiplexer_29 (
    .in0(xor_12_out[15:12]), .in1(xor_12_out[19:16]), .out(multiplexer_29_out), .sel(in_1));
  Multiplexer #(.width(4)) multiplexer_30 (
    .in0(xor_12_out[19:16]), .in1(xor_12_out[23:20]), .out(multiplexer_30_out), .sel(in_1));
  Multiplexer #(.width(4)) multiplexer_31 (
    .in0(xor_12_out[23:20]), .in1(xor_12_out[27:24]), .out(multiplexer_31_out), .sel(in_1));
  Multiplexer #(.width(4)) multiplexer_32 (
    .in0(xor_12_out[27:24]), .in1(xor_12_out[31:28]), .out(multiplexer_32_out), .sel(in_1));
  Multiplexer #(.width(4)) multiplexer_33 (
    .in0(xor_12_out[31:28]), .in1(xor_13_out[3:0]), .out(multiplexer_33_out), .sel(in_1));
  Multiplexer #(.width(4)) multiplexer_34 (
    .in0(xor_13_out[3:0]), .in1(xor_13_out[7:4]), .out(multiplexer_34_out), .sel(in_1));
  Multiplexer #(.width(4)) multiplexer_35 (
    .in0(xor_13_out[7:4]), .in1(xor_13_out[11:8]), .out(multiplexer_35_out), .sel(in_1));
  Multiplexer #(.width(4)) multiplexer_36 (
    .in0(xor_13_out[11:8]), .in1(xor_13_out[15:12]), .out(multiplexer_36_out), .sel(in_1));
  Multiplexer #(.width(4)) multiplexer_37 (
    .in0(xor_13_out[15:12]), .in1(xor_13_out[19:16]), .out(multiplexer_37_out), .sel(in_1));
  Multiplexer #(.width(4)) multiplexer_38 (
    .in0(xor_13_out[19:16]), .in1(xor_13_out[23:20]), .out(multiplexer_38_out), .sel(in_1));
  Multiplexer #(.width(4)) multiplexer_39 (
    .in0(xor_13_out[23:20]), .in1(xor_13_out[27:24]), .out(multiplexer_39_out), .sel(in_1));
  Multiplexer #(.width(4)) multiplexer_40 (
    .in0(xor_13_out[27:24]), .in1(xor_13_out[31:28]), .out(multiplexer_40_out), .sel(in_1));
  Multiplexer #(.width(4)) multiplexer_41 (
    .in0(xor_13_out[31:28]), .in1(xor_14_out[3:0]), .out(multiplexer_41_out), .sel(in_1));
  Multiplexer #(.width(4)) multiplexer_42 (
    .in0(xor_14_out[3:0]), .in1(xor_14_out[7:4]), .out(multiplexer_42_out), .sel(in_1));
  Multiplexer #(.width(4)) multiplexer_43 (
    .in0(xor_14_out[7:4]), .in1(xor_14_out[11:8]), .out(multiplexer_43_out), .sel(in_1));
  Multiplexer #(.width(4)) multiplexer_44 (
    .in0(xor_14_out[11:8]), .in1(xor_14_out[15:12]), .out(multiplexer_44_out), .sel(in_1));
  Multiplexer #(.width(4)) multiplexer_45 (
    .in0(xor_14_out[15:12]), .in1(xor_14_out[19:16]), .out(multiplexer_45_out), .sel(in_1));
  Multiplexer #(.width(4)) multiplexer_46 (
    .in0(xor_14_out[19:16]), .in1(xor_14_out[23:20]), .out(multiplexer_46_out), .sel(in_1));
  Multiplexer #(.width(4)) multiplexer_47 (
    .in0(xor_14_out[23:20]), .in1(xor_14_out[27:24]), .out(multiplexer_47_out), .sel(in_1));
  Multiplexer #(.width(4)) multiplexer_48 (
    .in0(xor_14_out[27:24]), .in1(xor_14_out[31:28]), .out(multiplexer_48_out), .sel(in_1));
  Multiplexer #(.width(4)) multiplexer_49 (
    .in0(xor_14_out[31:28]), .in1(xor_15_out[3:0]), .out(multiplexer_49_out), .sel(in_1));
  Multiplexer #(.width(4)) multiplexer_50 (
    .in0(xor_15_out[3:0]), .in1(xor_15_out[7:4]), .out(multiplexer_50_out), .sel(in_1));
  Multiplexer #(.width(4)) multiplexer_51 (
    .in0(xor_15_out[7:4]), .in1(xor_15_out[11:8]), .out(multiplexer_51_out), .sel(in_1));
  Multiplexer #(.width(4)) multiplexer_52 (
    .in0(xor_15_out[11:8]), .in1(xor_15_out[15:12]), .out(multiplexer_52_out), .sel(in_1));
  Multiplexer #(.width(4)) multiplexer_53 (
    .in0(xor_15_out[15:12]), .in1(xor_15_out[19:16]), .out(multiplexer_53_out), .sel(in_1));
  Multiplexer #(.width(4)) multiplexer_54 (
    .in0(xor_15_out[19:16]), .in1(xor_15_out[23:20]), .out(multiplexer_54_out), .sel(in_1));
  Multiplexer #(.width(4)) multiplexer_55 (
    .in0(xor_15_out[23:20]), .in1(xor_15_out[27:24]), .out(multiplexer_55_out), .sel(in_1));
  Multiplexer #(.width(4)) multiplexer_56 (
    .in0(xor_15_out[27:24]), .in1(xor_15_out[31:28]), .out(multiplexer_56_out), .sel(in_1));
  Multiplexer #(.width(4)) multiplexer_57 (
    .in0(xor_15_out[31:28]), .in1(xor_16_out[3:0]), .out(multiplexer_57_out), .sel(in_1));
  Multiplexer #(.width(4)) multiplexer_58 (
    .in0(xor_16_out[3:0]), .in1(xor_16_out[7:4]), .out(multiplexer_58_out), .sel(in_1));
  Multiplexer #(.width(4)) multiplexer_59 (
    .in0(xor_16_out[7:4]), .in1(xor_16_out[11:8]), .out(multiplexer_59_out), .sel(in_1));
  Multiplexer #(.width(4)) multiplexer_60 (
    .in0(xor_16_out[11:8]), .in1(xor_16_out[15:12]), .out(multiplexer_60_out), .sel(in_1));
  Multiplexer #(.width(4)) multiplexer_61 (
    .in0(xor_16_out[15:12]), .in1(xor_16_out[19:16]), .out(multiplexer_61_out), .sel(in_1));
  Multiplexer #(.width(4)) multiplexer_62 (
    .in0(xor_16_out[19:16]), .in1(xor_16_out[23:20]), .out(multiplexer_62_out), .sel(in_1));
  Multiplexer #(.width(4)) multiplexer_63 (
    .in0(xor_16_out[23:20]), .in1(xor_16_out[27:24]), .out(multiplexer_63_out), .sel(in_1));
  Multiplexer #(.width(4)) multiplexer_64 (
    .in0(xor_16_out[27:24]), .in1(xor_16_out[31:28]), .out(multiplexer_64_out), .sel(in_1));
  Multiplexer #(.width(4)) multiplexer_65 (
    .in0(xor_16_out[31:28]), .in1(xor_17_out[3:0]), .out(multiplexer_65_out), .sel(in_1));
  Multiplexer #(.width(4)) multiplexer_66 (
    .in0(xor_17_out[3:0]), .in1(xor_17_out[7:4]), .out(multiplexer_66_out), .sel(in_1));
  Multiplexer #(.width(4)) multiplexer_67 (
    .in0(xor_17_out[7:4]), .in1(xor_17_out[11:8]), .out(multiplexer_67_out), .sel(in_1));
  Multiplexer #(.width(4)) multiplexer_68 (
    .in0(xor_17_out[11:8]), .in1(xor_17_out[15:12]), .out(multiplexer_68_out), .sel(in_1));
  Multiplexer #(.width(4)) multiplexer_69 (
    .in0(xor_17_out[15:12]), .in1(xor_17_out[19:16]), .out(multiplexer_69_out), .sel(in_1));
  Multiplexer #(.width(4)) multiplexer_70 (
    .in0(xor_17_out[19:16]), .in1(xor_17_out[23:20]), .out(multiplexer_70_out), .sel(in_1));
  Multiplexer #(.width(4)) multiplexer_71 (
    .in0(xor_17_out[23:20]), .in1(xor_17_out[27:24]), .out(multiplexer_71_out), .sel(in_1));
  Multiplexer #(.width(4)) multiplexer_72 (
    .in0(xor_17_out[27:24]), .in1(xor_17_out[31:28]), .out(multiplexer_72_out), .sel(in_1));
  Multiplexer #(.width(4)) multiplexer_73 (
    .in0(xor_17_out[31:28]), .in1(xor_1_out[3:0]), .out(multiplexer_73_out), .sel(in_1));
  Multiplexer #(.width(4)) multiplexer_74 (
    .in0(xor_1_out[3:0]), .in1(xor_1_out[7:4]), .out(multiplexer_74_out), .sel(in_1));
  Multiplexer #(.width(4)) multiplexer_75 (
    .in0(xor_1_out[7:4]), .in1(xor_1_out[11:8]), .out(multiplexer_75_out), .sel(in_1));
  Multiplexer #(.width(4)) multiplexer_76 (
    .in0(xor_1_out[11:8]), .in1(xor_1_out[15:12]), .out(multiplexer_76_out), .sel(in_1));
  Multiplexer #(.width(4)) multiplexer_77 (
    .in0(xor_1_out[15:12]), .in1(xor_1_out[19:16]), .out(multiplexer_77_out), .sel(in_1));
  Multiplexer #(.width(4)) multiplexer_78 (
    .in0(xor_1_out[19:16]), .in1(xor_1_out[23:20]), .out(multiplexer_78_out), .sel(in_1));
  Multiplexer #(.width(4)) multiplexer_79 (
    .in0(xor_1_out[23:20]), .in1(xor_1_out[27:24]), .out(multiplexer_79_out), .sel(in_1));
  Multiplexer #(.width(4)) multiplexer_80 (
    .in0(xor_1_out[27:24]), .in1(xor_1_out[31:28]), .out(multiplexer_80_out), .sel(in_1));
  Multiplexer #(.width(4)) multiplexer_81 (
    .in0(xor_1_out[31:28]), .in1(xor_2_out[3:0]), .out(multiplexer_81_out), .sel(in_1));
  Multiplexer #(.width(4)) multiplexer_82 (
    .in0(xor_2_out[3:0]), .in1(xor_2_out[7:4]), .out(multiplexer_82_out), .sel(in_1));
  Multiplexer #(.width(4)) multiplexer_83 (
    .in0(xor_2_out[7:4]), .in1(xor_2_out[11:8]), .out(multiplexer_83_out), .sel(in_1));
  Multiplexer #(.width(4)) multiplexer_84 (
    .in0(xor_2_out[11:8]), .in1(xor_2_out[15:12]), .out(multiplexer_84_out), .sel(in_1));
  Multiplexer #(.width(4)) multiplexer_85 (
    .in0(xor_2_out[15:12]), .in1(xor_2_out[19:16]), .out(multiplexer_85_out), .sel(in_1));
  Multiplexer #(.width(4)) multiplexer_86 (
    .in0(xor_2_out[19:16]), .in1(xor_2_out[23:20]), .out(multiplexer_86_out), .sel(in_1));
  Multiplexer #(.width(4)) multiplexer_87 (
    .in0(xor_2_out[23:20]), .in1(xor_2_out[27:24]), .out(multiplexer_87_out), .sel(in_1));
  Multiplexer #(.width(4)) multiplexer_88 (
    .in0(xor_2_out[27:24]), .in1(xor_2_out[31:28]), .out(multiplexer_88_out), .sel(in_1));
  Multiplexer #(.width(4)) multiplexer_89 (
    .in0(xor_2_out[31:28]), .in1(xor_3_out[3:0]), .out(multiplexer_89_out), .sel(in_1));
  Multiplexer #(.width(4)) multiplexer_90 (
    .in0(xor_3_out[3:0]), .in1(xor_3_out[7:4]), .out(multiplexer_90_out), .sel(in_1));
  Multiplexer #(.width(4)) multiplexer_91 (
    .in0(xor_3_out[7:4]), .in1(xor_3_out[11:8]), .out(multiplexer_91_out), .sel(in_1));
  Multiplexer #(.width(4)) multiplexer_92 (
    .in0(xor_3_out[11:8]), .in1(xor_3_out[15:12]), .out(multiplexer_92_out), .sel(in_1));
  Multiplexer #(.width(4)) multiplexer_93 (
    .in0(xor_3_out[15:12]), .in1(xor_3_out[19:16]), .out(multiplexer_93_out), .sel(in_1));
  Multiplexer #(.width(4)) multiplexer_94 (
    .in0(xor_3_out[19:16]), .in1(xor_3_out[23:20]), .out(multiplexer_94_out), .sel(in_1));
  Multiplexer #(.width(4)) multiplexer_95 (
    .in0(xor_3_out[23:20]), .in1(xor_3_out[27:24]), .out(multiplexer_95_out), .sel(in_1));
  Multiplexer #(.width(4)) multiplexer_96 (
    .in0(xor_3_out[27:24]), .in1(xor_3_out[31:28]), .out(multiplexer_96_out), .sel(in_1));
  Multiplexer #(.width(4)) multiplexer_97 (
    .in0(xor_3_out[31:28]), .in1(xor_4_out[3:0]), .out(multiplexer_97_out), .sel(in_1));
  Multiplexer #(.width(4)) multiplexer_98 (
    .in0(xor_4_out[3:0]), .in1(xor_4_out[7:4]), .out(multiplexer_98_out), .sel(in_1));
  Multiplexer #(.width(4)) multiplexer_99 (
    .in0(xor_4_out[7:4]), .in1(xor_4_out[11:8]), .out(multiplexer_99_out), .sel(in_1));
  Multiplexer #(.width(4)) multiplexer_100 (
    .in0(xor_4_out[11:8]), .in1(xor_4_out[15:12]), .out(multiplexer_100_out), .sel(in_1));
  Multiplexer #(.width(4)) multiplexer_101 (
    .in0(xor_4_out[15:12]), .in1(xor_4_out[19:16]), .out(multiplexer_101_out), .sel(in_1));
  Multiplexer #(.width(4)) multiplexer_102 (
    .in0(xor_4_out[19:16]), .in1(xor_4_out[23:20]), .out(multiplexer_102_out), .sel(in_1));
  Multiplexer #(.width(4)) multiplexer_103 (
    .in0(xor_4_out[23:20]), .in1(xor_4_out[27:24]), .out(multiplexer_103_out), .sel(in_1));
  Multiplexer #(.width(4)) multiplexer_104 (
    .in0(xor_4_out[27:24]), .in1(xor_4_out[31:28]), .out(multiplexer_104_out), .sel(in_1));
  Multiplexer #(.width(4)) multiplexer_105 (
    .in0(xor_4_out[31:28]), .in1(xor_5_out[3:0]), .out(multiplexer_105_out), .sel(in_1));
  Multiplexer #(.width(4)) multiplexer_106 (
    .in0(xor_5_out[3:0]), .in1(xor_5_out[7:4]), .out(multiplexer_106_out), .sel(in_1));
  Multiplexer #(.width(4)) multiplexer_107 (
    .in0(xor_5_out[7:4]), .in1(xor_5_out[11:8]), .out(multiplexer_107_out), .sel(in_1));
  Multiplexer #(.width(4)) multiplexer_108 (
    .in0(xor_5_out[11:8]), .in1(xor_5_out[15:12]), .out(multiplexer_108_out), .sel(in_1));
  Multiplexer #(.width(4)) multiplexer_109 (
    .in0(xor_5_out[15:12]), .in1(xor_5_out[19:16]), .out(multiplexer_109_out), .sel(in_1));
  Multiplexer #(.width(4)) multiplexer_110 (
    .in0(xor_5_out[19:16]), .in1(xor_5_out[23:20]), .out(multiplexer_110_out), .sel(in_1));
  Multiplexer #(.width(4)) multiplexer_111 (
    .in0(xor_5_out[23:20]), .in1(xor_5_out[27:24]), .out(multiplexer_111_out), .sel(in_1));
  Multiplexer #(.width(4)) multiplexer_112 (
    .in0(xor_5_out[27:24]), .in1(xor_5_out[31:28]), .out(multiplexer_112_out), .sel(in_1));
  Multiplexer #(.width(4)) multiplexer_113 (
    .in0(xor_5_out[31:28]), .in1(xor_6_out[3:0]), .out(multiplexer_113_out), .sel(in_1));
  Multiplexer #(.width(4)) multiplexer_114 (
    .in0(xor_6_out[3:0]), .in1(xor_6_out[7:4]), .out(multiplexer_114_out), .sel(in_1));
  Multiplexer #(.width(4)) multiplexer_115 (
    .in0(xor_6_out[7:4]), .in1(xor_6_out[11:8]), .out(multiplexer_115_out), .sel(in_1));
  Multiplexer #(.width(4)) multiplexer_116 (
    .in0(xor_6_out[11:8]), .in1(xor_6_out[15:12]), .out(multiplexer_116_out), .sel(in_1));
  Multiplexer #(.width(4)) multiplexer_117 (
    .in0(xor_6_out[15:12]), .in1(xor_6_out[19:16]), .out(multiplexer_117_out), .sel(in_1));
  Multiplexer #(.width(4)) multiplexer_118 (
    .in0(xor_6_out[19:16]), .in1(xor_6_out[23:20]), .out(multiplexer_118_out), .sel(in_1));
  Multiplexer #(.width(4)) multiplexer_119 (
    .in0(xor_6_out[23:20]), .in1(xor_6_out[27:24]), .out(multiplexer_119_out), .sel(in_1));
  Multiplexer #(.width(4)) multiplexer_120 (
    .in0(xor_6_out[27:24]), .in1(xor_6_out[31:28]), .out(multiplexer_120_out), .sel(in_1));
  Multiplexer #(.width(4)) multiplexer_121 (
    .in0(xor_6_out[31:28]), .in1(xor_7_out[3:0]), .out(multiplexer_121_out), .sel(in_1));
  Multiplexer #(.width(4)) multiplexer_122 (
    .in0(xor_7_out[3:0]), .in1(xor_7_out[7:4]), .out(multiplexer_122_out), .sel(in_1));
  Multiplexer #(.width(4)) multiplexer_123 (
    .in0(xor_7_out[7:4]), .in1(xor_7_out[11:8]), .out(multiplexer_123_out), .sel(in_1));
  Multiplexer #(.width(4)) multiplexer_124 (
    .in0(xor_7_out[11:8]), .in1(xor_7_out[15:12]), .out(multiplexer_124_out), .sel(in_1));
  Multiplexer #(.width(4)) multiplexer_125 (
    .in0(xor_7_out[15:12]), .in1(xor_7_out[19:16]), .out(multiplexer_125_out), .sel(in_1));
  Multiplexer #(.width(4)) multiplexer_126 (
    .in0(xor_7_out[19:16]), .in1(xor_7_out[23:20]), .out(multiplexer_126_out), .sel(in_1));
  Multiplexer #(.width(4)) multiplexer_127 (
    .in0(xor_7_out[23:20]), .in1(xor_7_out[27:24]), .out(multiplexer_127_out), .sel(in_1));
  Multiplexer #(.width(4)) multiplexer_128 (
    .in0(xor_7_out[27:24]), .in1(xor_7_out[31:28]), .out(multiplexer_128_out), .sel(in_1));
  Multiplexer #(.width(4)) multiplexer_129 (
    .in0(xor_7_out[31:28]), .in1(xor_8_out[3:0]), .out(multiplexer_129_out), .sel(in_1));
  Multiplexer #(.width(4)) multiplexer_130 (
    .in0(xor_8_out[3:0]), .in1(xor_8_out[7:4]), .out(multiplexer_130_out), .sel(in_1));
  Multiplexer #(.width(4)) multiplexer_131 (
    .in0(xor_8_out[7:4]), .in1(xor_8_out[11:8]), .out(multiplexer_131_out), .sel(in_1));
  Multiplexer #(.width(4)) multiplexer_132 (
    .in0(xor_8_out[11:8]), .in1(xor_8_out[15:12]), .out(multiplexer_132_out), .sel(in_1));
  Multiplexer #(.width(4)) multiplexer_133 (
    .in0(xor_8_out[15:12]), .in1(xor_8_out[19:16]), .out(multiplexer_133_out), .sel(in_1));
  Multiplexer #(.width(4)) multiplexer_134 (
    .in0(xor_8_out[19:16]), .in1(xor_8_out[23:20]), .out(multiplexer_134_out), .sel(in_1));
  Multiplexer #(.width(4)) multiplexer_135 (
    .in0(xor_8_out[23:20]), .in1(xor_8_out[27:24]), .out(multiplexer_135_out), .sel(in_1));
  Multiplexer #(.width(4)) multiplexer_136 (
    .in0(xor_8_out[27:24]), .in1(xor_8_out[31:28]), .out(multiplexer_136_out), .sel(in_1));
  xor xor_18 (or_1_out[3], multiplexer_1_out[0], multiplexer_1_out[1]);
  xor xor_19 (xor_19_out, multiplexer_1_out[2], multiplexer_1_out[3]);
  and and_1 (or_1_out[2], xor_19_out, multiplexer_2_out[0]);
  or or_1 (or_1_out[0], xor_19_out, multiplexer_2_out[1]);
  assign xor_20_out = undriven_36 ^ {undriven_35, multiplexer_7_out, multiplexer_6_out, multiplexer_5_out, multiplexer_4_out, multiplexer_3_out, or_1_out[3:2], multiplexer_2_out[1], or_1_out[0], multiplexer_1_out};  // XOR_Gate xor_20, 32 bits wide
  assign xor_21_out = undriven_37 ^ {multiplexer_16_out, multiplexer_15_out, multiplexer_14_out, multiplexer_13_out, multiplexer_12_out, multiplexer_11_out, multiplexer_10_out, multiplexer_9_out};  // XOR_Gate xor_21, 32 bits wide
  assign xor_22_out = undriven_38 ^ {multiplexer_24_out, multiplexer_23_out, multiplexer_22_out, multiplexer_21_out, multiplexer_20_out, multiplexer_19_out, multiplexer_18_out, multiplexer_17_out};  // XOR_Gate xor_22, 32 bits wide
  assign xor_23_out = undriven_39 ^ {multiplexer_32_out, multiplexer_31_out, multiplexer_30_out, multiplexer_29_out, multiplexer_28_out, multiplexer_27_out, multiplexer_26_out, multiplexer_25_out};  // XOR_Gate xor_23, 32 bits wide
  assign xor_24_out = undriven_40 ^ {multiplexer_40_out, multiplexer_39_out, multiplexer_38_out, multiplexer_37_out, multiplexer_36_out, multiplexer_35_out, multiplexer_34_out, multiplexer_33_out};  // XOR_Gate xor_24, 32 bits wide
  assign xor_25_out = undriven_41 ^ {multiplexer_48_out, multiplexer_47_out, multiplexer_46_out, multiplexer_45_out, multiplexer_44_out, multiplexer_43_out, multiplexer_42_out, multiplexer_41_out};  // XOR_Gate xor_25, 32 bits wide
  assign xor_26_out = undriven_42 ^ {multiplexer_56_out, multiplexer_55_out, multiplexer_54_out, multiplexer_53_out, multiplexer_52_out, multiplexer_51_out, multiplexer_50_out, multiplexer_49_out};  // XOR_Gate xor_26, 32 bits wide
  assign xor_27_out = undriven_43 ^ {multiplexer_64_out, multiplexer_63_out, multiplexer_62_out, multiplexer_61_out, multiplexer_60_out, multiplexer_59_out, multiplexer_58_out, multiplexer_57_out};  // XOR_Gate xor_27, 32 bits wide
  assign xor_28_out = undriven_44 ^ {multiplexer_72_out, multiplexer_71_out, multiplexer_70_out, multiplexer_69_out, multiplexer_68_out, multiplexer_67_out, multiplexer_66_out, multiplexer_65_out};  // XOR_Gate xor_28, 32 bits wide
  assign xor_29_out = undriven_45 ^ {multiplexer_80_out, multiplexer_79_out, multiplexer_78_out, multiplexer_77_out, multiplexer_76_out, multiplexer_75_out, multiplexer_74_out, multiplexer_73_out};  // XOR_Gate xor_29, 32 bits wide
  assign xor_30_out = undriven_46 ^ {multiplexer_88_out, multiplexer_87_out, multiplexer_86_out, multiplexer_85_out, multiplexer_84_out, multiplexer_83_out, multiplexer_82_out, multiplexer_81_out};  // XOR_Gate xor_30, 32 bits wide
  assign xor_31_out = undriven_47 ^ {multiplexer_96_out, multiplexer_95_out, multiplexer_94_out, multiplexer_93_out, multiplexer_92_out, multiplexer_91_out, multiplexer_90_out, multiplexer_89_out};  // XOR_Gate xor_31, 32 bits wide
  assign xor_32_out = undriven_48 ^ {multiplexer_104_out, multiplexer_103_out, multiplexer_102_out, multiplexer_101_out, multiplexer_100_out, multiplexer_99_out, multiplexer_98_out, multiplexer_97_out};  // XOR_Gate xor_32, 32 bits wide
  assign xor_33_out = undriven_49 ^ {multiplexer_112_out, multiplexer_111_out, multiplexer_110_out, multiplexer_109_out, multiplexer_108_out, multiplexer_107_out, multiplexer_106_out, multiplexer_105_out};  // XOR_Gate xor_33, 32 bits wide
  assign xor_34_out = undriven_50 ^ {multiplexer_120_out, multiplexer_119_out, multiplexer_118_out, multiplexer_117_out, multiplexer_116_out, multiplexer_115_out, multiplexer_114_out, multiplexer_113_out};  // XOR_Gate xor_34, 32 bits wide
  assign xor_35_out = undriven_51 ^ {multiplexer_128_out, multiplexer_127_out, multiplexer_126_out, multiplexer_125_out, multiplexer_124_out, multiplexer_123_out, multiplexer_122_out, multiplexer_121_out};  // XOR_Gate xor_35, 32 bits wide
  assign xor_36_out = undriven_52 ^ {multiplexer_136_out, multiplexer_135_out, multiplexer_134_out, multiplexer_133_out, multiplexer_132_out, multiplexer_131_out, multiplexer_130_out, multiplexer_129_out};  // XOR_Gate xor_36, 32 bits wide
  assign not_1_out = ~xor_32_out;  // NOT_Gate not_1, 32 bits wide
  assign not_2_out = ~xor_34_out;  // NOT_Gate not_2, 32 bits wide
  assign not_3_out = ~xor_36_out;  // NOT_Gate not_3, 32 bits wide

  // Notes on the sheet:
  //   00110111
  //   01111101
  //   00110111
  //   01111010
  //   00110111
  //   01011010
  //   00110111
  //   01111010
  //   00110111
  //   01011111
  //   00110111
  //   01100100
  //   00110111
  //   01100101
  //   00110111
  //   01110010 
  //   00110111
  //   00110111
  //   00110111
  //   01101001
  //   00110111
  //   01110100
  //   00110111
  //   01011111
  //   00110111
  //   01101001
  //   00110111
  //   01111011
  //   00110111
  //   01010111
  //   00110111
  //   01000011
  //   00110111
  //   01001110
  //   00111001
  //   00111001
  //   00111001
  //   00111001
  //   00111001
  //   00111001
  //   00111001
  //   00111001
  //   00111001
  //   00111001
  //   00111001
  //   00111001
  //   00111001
  //   00111001
  //   00111001
  //   00111001
  //   00111001
  //   OUTPUT
endmodule
